# Fritzing sketch cad (saved by Fritzing 0.9.3b)

parts:
  LED1 = smd LED [color="Yellow (592nm)" package="1206 [SMD]"]
  Componente1 = Arduino Pro Mini (5V)
  R1 = Resistor [tolerance=±5% resistance=320 package="0402 [SMD]"]
  U1 = RELAY [package=relay-jzc]

nets:
  N1: LED1.anode, Componente1.D4, U1.COIL2
  N2: Componente1.GND, R1.Pin_0, U1.NO

notes:
  Fonte
  IN: 127V AC
  OUT: 5V DC
  Neutro
  Fase para a carga
  Fase
